// Logisim project Real_Alu.circ as structural Verilog
module Mux_4bit (
  input  [3:0] S,
  input  _0,
  input  _1,
  input  _2,
  input  _3,
  input  _4,
  input  _5,
  input  _6,
  input  _7,
  input  _8,
  input  _9,
  input  _10,
  input  _11,
  input  _12,
  input  _13,
  input  _14,
  input  _15,
  output out_18
);

  wire _0_t, _1_t, _2_t, _3_t, _4_t, _5_t, _6_t, _7_t, _8_t, _9_t, _10_t, _11_t, _12_t, _13_t, _14_t, _15_t,
       S00, S11, S22, S33;

  not not_1 (S33, S[3]);
  not not_2 (S22, S[2]);
  not not_3 (S11, S[1]);
  not not_4 (S00, S[0]);
  and and_1 (_0_t, S00, S11, S22, S33, _0);
  and and_2 (_1_t, S[0], S11, S22, S33, _1);
  and and_3 (_2_t, S00, S[1], S22, S33, _2);
  and and_4 (_3_t, S[0], S[1], S22, S33, _3);
  and and_5 (_4_t, S00, S11, S[2], S33, _4);
  and and_6 (_5_t, S[0], S11, S[2], S33, _5);
  and and_7 (_6_t, S00, S[1], S[2], S33, _6);
  and and_8 (_7_t, S[0], S[1], S[2], S33, _7);
  and and_9 (_8_t, S00, S11, S22, S[3], _8);
  and and_10 (_9_t, S[0], S11, S22, S[3], _9);
  and and_11 (_10_t, S00, S[1], S22, S[3], _10);
  and and_12 (_11_t, S[0], S[1], S22, S[3], _11);
  and and_13 (_12_t, S00, S11, S[2], S[3], _12);
  and and_14 (_13_t, S[0], S11, S[2], S[3], _13);
  and and_15 (_14_t, S00, S[1], S[2], S[3], _14);
  and and_16 (_15_t, S[0], S[1], S[2], S[3], _15);
  or or_1 (out_18, _0_t, _1_t, _2_t, _3_t, _4_t, _5_t, _6_t, _7_t, _8_t, _9_t, _10_t, _11_t, _12_t, _13_t, _14_t, _15_t);
endmodule

module And (
  input  [7:0] a,
  input  [7:0] b,
  output [7:0] out_3,
  output out_4
);

  assign out_3 = a & b;  // AND_Gate and_1, 8 bits wide
  nor nor_1 (out_4, out_3[7], out_3[6], out_3[5], out_3[4], out_3[3], out_3[2], out_3[1], out_3[0]);
endmodule

module Or (
  input  [7:0] a,
  input  [7:0] b,
  output [7:0] out_3,
  output z
);

  assign out_3 = a | b;  // OR_Gate or_1, 8 bits wide
  nor nor_1 (z, out_3[7], out_3[6], out_3[5], out_3[4], out_3[3], out_3[2], out_3[1], out_3[0]);
endmodule

module Not_B (
  input  [7:0] B,
  output [7:0] out_2,
  output z
);

  assign out_2 = ~B;  // NOT_Gate not_1, 8 bits wide
  nor nor_1 (z, out_2[7], out_2[6], out_2[5], out_2[4], out_2[3], out_2[2], out_2[1], out_2[0]);
endmodule

module LSR_B (
  input  [7:0] B,
  output [7:0] out_2,
  output Carry,
  output Z,
  output P_N
);

  nor nor_1 (Z, B[0], B[1], B[2], B[3], B[4], B[5], B[6], B[7]);

  assign Carry = B[7];
  assign out_2 = {B[6:0], 1'b0};
  assign P_N = B[7];
endmodule

module LSL_B (
  input  [7:0] B,
  output Carry,
  output [7:0] out_3,
  output Z,
  output P_N
);

  nor nor_1 (Z, B[0], B[1], B[2], B[3], B[4], B[5], B[6], B[7]);

  assign Carry = B[0];
  assign out_3 = {1'b0, B[7:1]};
  assign P_N = B[7];
endmodule

module decoder (
  input  in_1,
  input  in_2,
  input  in_3,
  input  in_4,
  output [15:0] out_5
);

  wire not_1_out, not_2_out, not_3_out, not_4_out;

  not not_1 (not_1_out, in_3);
  not not_2 (not_2_out, in_1);
  not not_3 (not_3_out, in_2);
  not not_4 (not_4_out, in_4);
  and and_1 (out_5[0], not_4_out, not_1_out, not_3_out, not_2_out);
  and and_2 (out_5[1], in_4, not_1_out, not_3_out, not_2_out);
  and and_3 (out_5[2], not_4_out, in_3, not_3_out, not_2_out);
  and and_4 (out_5[3], in_4, in_3, not_3_out, not_2_out);
  and and_5 (out_5[4], not_4_out, not_1_out, in_2, not_2_out);
  and and_6 (out_5[5], in_4, not_1_out, in_2, not_2_out);
  and and_7 (out_5[6], not_4_out, in_3, in_2, not_2_out);
  and and_8 (out_5[7], in_4, in_3, in_2, not_2_out);
  and and_9 (out_5[8], not_4_out, not_1_out, not_3_out, in_1);
  and and_10 (out_5[9], in_4, not_1_out, not_3_out, in_1);
  and and_11 (out_5[10], not_4_out, in_3, not_3_out, in_1);
  and and_12 (out_5[11], in_4, in_3, not_3_out, in_1);
  and and_13 (out_5[12], not_4_out, not_1_out, in_2, in_1);
  and and_14 (out_5[13], in_4, not_1_out, in_2, in_1);
  and and_15 (out_5[14], not_4_out, in_3, in_2, in_1);
  and and_16 (out_5[15], in_4, in_3, in_2, in_1);
endmodule

module Full_Adder (
  input  C0,
  input  a,
  input  b,
  output S,
  output C1
);

  wire and_1_out, and_2_out, and_3_out, xor_1_out;

  xor xor_1 (xor_1_out, a, b);
  and and_1 (and_1_out, C0, a);
  and and_2 (and_2_out, a, b);
  and and_3 (and_3_out, C0, b);
  xor xor_2 (S, xor_1_out, C0);
  or or_1 (C1, and_1_out, and_2_out, and_3_out);
endmodule

module Adder_8bit (
  input  a0,
  input  b0,
  input  c0,
  input  a1,
  input  b1,
  input  a2,
  input  b2,
  input  a3,
  input  b3,
  output s0,
  output s1,
  output s2,
  output s3,
  output C
);

  wire full_adder_1_c1, full_adder_2_c1, full_adder_3_c1;

  Full_Adder full_adder_1 (.S(s0), .C1(full_adder_1_c1), .C0(b0), .a(a0), .b(c0));
  Full_Adder full_adder_2 (.S(s1), .C1(full_adder_2_c1), .C0(b1), .a(a1), .b(full_adder_1_c1));
  Full_Adder full_adder_3 (.S(s2), .C1(full_adder_3_c1), .C0(b2), .a(a2), .b(full_adder_2_c1));
  Full_Adder full_adder_4 (.S(s3), .C1(C), .C0(b3), .a(a3), .b(full_adder_3_c1));
endmodule

module Adder (
  input  a7,
  input  b7,
  input  a6,
  input  b6,
  input  a5,
  input  b5,
  input  a4,
  input  b4,
  input  a3,
  input  b3,
  input  a2,
  input  b2,
  input  a1,
  input  b1,
  input  a0,
  input  b0,
  input  in_17,
  output overflow,
  output s7,
  output s6,
  output s5,
  output s4,
  output s3,
  output s2,
  output s1,
  output s0
);

  wire adder_8bit_2_c;

  Adder_8bit adder_8bit_1 (
    .s0(s7), .s1(s6), .s2(s5), .s3(s4), .a0(a7), .a1(a6), .a2(a5), .a3(a4), .b0(b4), .b1(b5), .b2(b6),
    .b3(b7), .c0(adder_8bit_2_c), .C(overflow));
  Adder_8bit adder_8bit_2 (
    .s0(s0), .s1(s1), .s2(s2), .s3(s3), .a0(a3), .a1(a2), .a2(a1), .a3(a0), .b0(b0), .b1(b1), .b2(b2),
    .b3(b3), .c0(in_17), .C(adder_8bit_2_c));
endmodule

module Half_Adder (
  input  a,
  input  b,
  output S,
  output out_4
);

  xor xor_1 (S, a, b);
  and and_1 (out_4, a, b);
endmodule

module Complemento_2 (
  input  [7:0] in_1,
  output C,
  output [7:0] out_3
);

  wire half_adder_2_out_4, half_adder_3_out_4, half_adder_4_out_4, half_adder_5_out_4, half_adder_6_out_4,
       half_adder_7_out_4, half_adder_8_out_4;
  wire [7:0] not_1_out;

  assign not_1_out = ~in_1;  // NOT_Gate not_1, 8 bits wide
  Half_Adder half_adder_1 (.a(not_1_out[0]), .b(half_adder_2_out_4), .S(out_3[7]), .out_4(C));
  Half_Adder half_adder_2 (.a(not_1_out[1]), .b(half_adder_3_out_4), .S(out_3[6]), .out_4(half_adder_2_out_4));
  Half_Adder half_adder_3 (.a(not_1_out[2]), .b(half_adder_4_out_4), .S(out_3[5]), .out_4(half_adder_3_out_4));
  Half_Adder half_adder_4 (.a(not_1_out[3]), .b(half_adder_5_out_4), .S(out_3[4]), .out_4(half_adder_4_out_4));
  Half_Adder half_adder_5 (.a(not_1_out[4]), .b(half_adder_6_out_4), .S(out_3[3]), .out_4(half_adder_5_out_4));
  Half_Adder half_adder_6 (.a(not_1_out[5]), .b(half_adder_7_out_4), .S(out_3[2]), .out_4(half_adder_6_out_4));
  Half_Adder half_adder_7 (.a(not_1_out[6]), .b(half_adder_8_out_4), .S(out_3[1]), .out_4(half_adder_7_out_4));
  Half_Adder half_adder_8 (.a(1'b1), .b(not_1_out[7]), .S(out_3[0]), .out_4(half_adder_8_out_4));
endmodule

module Sottrattore (
  input  [7:0] B,
  input  [7:0] A,
  input  in_3,
  output [7:0] out_4,
  output out_5,
  output [7:0] out_6
);

  wire complemento_2_1_c;

  Adder adder_1 (
    .a7(A[0]), .a6(A[1]), .a5(A[2]), .a4(A[3]), .a3(A[4]), .a2(A[5]), .a1(A[6]), .a0(A[7]), .b7(out_4[0]),
    .b6(out_4[1]), .b5(out_4[2]), .b4(out_4[3]), .b3(out_4[4]), .b2(out_4[5]), .b1(out_4[6]), .b0(out_4[7]),
    .in_17(in_3), .overflow(out_5), .s7(out_6[7]), .s6(out_6[6]), .s5(out_6[5]), .s4(out_6[4]),
    .s3(out_6[3]), .s2(out_6[2]), .s1(out_6[1]), .s0(out_6[0]));
  Complemento_2 complemento_2_1 (.in_1(B), .C(complemento_2_1_c), .out_3(out_4));
  LED led_1 (.in(complemento_2_1_c));
endmodule

module Incremento (
  input  [7:0] A,
  input  in_2,
  output out_3,
  output [7:0] out_4
);

  Adder adder_1 (
    .a7(A[0]), .a6(A[1]), .a5(A[2]), .a4(A[3]), .a3(A[4]), .a2(A[5]), .a1(A[6]), .a0(A[7]), .b7(1'b0),
    .b6(1'b0), .b5(1'b0), .b4(1'b0), .b3(1'b0), .b2(1'b0), .b1(1'b0), .b0(1'b1), .in_17(in_2),
    .overflow(out_3), .s7(out_4[7]), .s6(out_4[6]), .s5(out_4[5]), .s4(out_4[4]), .s3(out_4[3]),
    .s2(out_4[2]), .s1(out_4[1]), .s0(out_4[0]));
endmodule
